// Logisim project cdlatch.circ as structural Verilog: 2 circuits, main circuit ms_sr_flip_flop
module C_D_latch (
  input  D,
  input  C,
  output Qbar,
  output Q
);

  wire nand_1_out, nand_2_out, not_1_out;

  not not_1 (not_1_out, D);
  nand nand_1 (nand_1_out, not_1_out, C);
  nand nand_2 (nand_2_out, C, D);
  nand nand_3 (Qbar, nand_1_out, Q);
  nand nand_4 (Q, Qbar, nand_2_out);
endmodule

module ms_sr_flip_flop (
  input  D,
  input  clk,
  output mid_Q,
  output Qbar,
  output Q
);

  wire not_1_out;

  not not_1 (not_1_out, clk);
  C_D_latch master_latch (.D(D), .C(not_1_out), .Q(mid_Q));  // open: Qbar
  C_D_latch slave_latch (.D(mid_Q), .C(clk), .Qbar(Qbar), .Q(Q));
endmodule
