// Logisim project csrlatch.circ as structural Verilog: 2 circuits, main circuit C_SR_latch
module C_SR_latch (
  input  R,
  input  C,
  input  S,
  output Qbar,
  output Q
);

  wire nand_1_out, nand_2_out;

  nand nand_1 (nand_1_out, R, C);
  nand nand_2 (nand_2_out, C, S);
  nand nand_3 (Qbar, nand_1_out, Q);
  nand nand_4 (Q, Qbar, nand_2_out);
endmodule

module MS_SR_flip_flop (
  input  R,
  input  clk,
  input  S,
  output Qbar,
  output Q,
  output mid_Q
);

  wire master_latch_qbar, not_1_out;

  not not_1 (not_1_out, clk);
  C_SR_latch master_latch (.R(R), .C(not_1_out), .S(S), .Qbar(master_latch_qbar), .Q(mid_Q));
  C_SR_latch slave_latch (.R(master_latch_qbar), .C(clk), .S(mid_Q), .Qbar(Qbar), .Q(Q));
endmodule
