// Logisim project srlatch.circ as structural Verilog: 1 circuit, main circuit SR_latch
module SR_latch (
  input  R,
  input  S,
  output Q,
  output Qbar
);

  nor nor_1 (Q, R, Qbar);
  nor nor_2 (Qbar, Q, S);
endmodule
